# Fritzing sketch analog-thermometer (saved by Fritzing 1.0.4)
breadboards: 1

parts:
  J1 = Basic Servo
  A1 = WeMos D1 Mini (reversed pins)
  RHT1 = Humidity and Temperature Sensor RHT03

nets:
  VCC: J1.vcc, A1.5V, RHT1.GND_2
  N1: J1.pulse, A1.D4
  N2: A1.G, RHT1.Data-signal
  N3: A1.D2, RHT1.GND_1

custom parts:
  WeMos D1 Mini (reversed pins): The D1 mini is a mini wifi board based on ESP-8266EX. (feb 2020 increase pcb hole sizes to 0.038 to accomadate .1 headers, change connectors from female to male, make connector id connector number rather than description) (May 2022 Reverse the pins (flip the board over so the pins are connected to the bottom of the board.)
