# Fritzing sketch persistent-credentials-microsd (saved by Fritzing 1.0.4)

parts:
  OLED_I2C1 = OLED 128x64 I2C Monochrome Display
  Bauteil1 = Arduino Uno (Rev3) - ICSP
  microSD1 = MicroSD Card Module

nets:
  N1: OLED_I2C1.SDA, Bauteil1.A4/SDA
  N2: OLED_I2C1.SCK, Bauteil1.A5/SCL
  N3: OLED_I2C1.VDD, Bauteil1.IOREF
  GND: OLED_I2C1.GND, Bauteil1.GND, microSD1.GND
  N4: Bauteil1.D10_PWM/SS, microSD1.CS
  N5: Bauteil1.D11_PWM/MOSI, microSD1.MOSI
  N6: Bauteil1.D12/MISO, microSD1.MISO
  N7: Bauteil1.D13/SCK, microSD1.SCK
  5V: Bauteil1.5V, microSD1.VCC
