# Fritzing sketch rfid-door-opener (saved by Fritzing 1.0.4)
breadboards: 1

parts:
  LED1 = smd LED [color="Red (633nm)" package="0603 [SMD]"]
  LED2 = smd LED [color="Green (570nm)" package="0603 [SMD]"]
  U1 = RFID RC522 SIP - 8 pins [chip_label="RFID RC522" package="SIP (Single Inline) [THT]"]
  J1 = Piezo Speaker
  Bauteil1 = Arduino Uno (Rev3) - ICSP

nets:
  N1: LED1.cathode, Bauteil1.D7
  GND: LED1.anode, LED2.anode, U1.GND, J1.pin1, Bauteil1.GND
  N2: LED2.cathode, Bauteil1.D8
  N3: U1.IRQ, Bauteil1.D4
  N4: U1.NSS, Bauteil1.D10_PWM/SS
  N5: U1.SCK, Bauteil1.D13/SCK
  N6: U1.MOSI, Bauteil1.D11_PWM/MOSI
  N7: U1.MISO, Bauteil1.D12/MISO
  N8: U1.RST, Bauteil1.D3_PWM
  VCC: U1.VCC, Bauteil1.5V
  N9: J1.pin2, Bauteil1.A0

notes:
  Plug in PCB for ESP32 NodeMCU D1 R32 and n ot for Arduino Uno R3

custom parts:
  RFID RC522 SIP - 8 pins: A SIP stand-in part for RFID RC522 . With 8 pins on a 300 mil single inline package (SIP) footprint.
