# Fritzing sketch timer-start-stop-reset (saved by Fritzing 1.0.4)
breadboards: 1

parts:
  S1 = Pushbutton [package="[THT]"]
  S2 = Pushbutton [package="[THT]"]
  S3 = Pushbutton [package="[THT]"]
  R1 = Resistor [tolerance=±5% power=0.25W resistance=220 package=THT]
  R2 = Resistor [tolerance=±5% power=0.25W resistance=220 package=THT]
  R3 = Resistor [tolerance=±5% power=0.25W resistance=220 package=THT]
  Bauteil1 = Arduino Mega 2560 (Rev3)
  HS420561K1 = HS420561K [part_number=HS420561K package="DIP (Dual Inline) [THT]"]

nets:
  N1: S1.Pin_1, S1.Pin_2, R1.Pin_1, Bauteil1.D18/TX1
  N2: S1.Pin_3, S1.Pin_4, S2.Pin_3, S2.Pin_4, S3.Pin_3, S3.Pin_4, Bauteil1.GND
  N3: S2.Pin_1, S2.Pin_2, R2.Pin_1, Bauteil1.D3_PWM
  N4: S3.Pin_1, S3.Pin_2, R3.Pin_1, Bauteil1.D2_PWM
  N5: R1.Pin_0, R2.Pin_0, R3.Pin_0, Bauteil1.5V
  N6: Bauteil1.D32, HS420561K1.pin_12
  N7: Bauteil1.D33, HS420561K1.pin_9
  N8: Bauteil1.D34, HS420561K1.pin_11
  N9: Bauteil1.D35, HS420561K1.pin_10
  N10: Bauteil1.D36, HS420561K1.pin8
  N11: Bauteil1.D37, HS420561K1.pin7
  N12: Bauteil1.D40, HS420561K1.pin6
  N13: Bauteil1.D41, HS420561K1.pin5
  N14: Bauteil1.D42, HS420561K1.pin1
  N15: Bauteil1.D43, HS420561K1.pin4
  N16: Bauteil1.D44, HS420561K1.pin2
  N17: Bauteil1.D45, HS420561K1.pin3

notes:
  Pin 2, 3 and 18 are capable of button hardware interrupts. You could use other pins but then you need to adapt the way of button pressure querieing.
